// Logisim project conputer.circ as structural Verilog: 1 circuit, main circuit main
module main (
  input  Run,
  input  Manual_mode,
  input  [7:0] in_3,
  input  Reset,
  input  [7:0] in_5,
  input  [7:0] in_6,
  input  [7:0] in_7,
  input  [7:0] in_8,
  input  [7:0] in_9,
  input  [7:0] in_10,
  input  [7:0] in_11
);

  wire add, adder_4_cout, adder_5_cout, and_1_out, and_2_out, and_3_out, and_4_out, and_5_out, and_6_out,
       and_7_out, and_8_out, and_10_out, and_13_out, and_15_out, brh, C, cal, clk, clock_1_out,
       comparator_1_eq, DB_WE, demultiplexer_1_out1, demultiplexer_1_out2, demultiplexer_1_out3,
       demultiplexer_1_out4, demultiplexer_1_out5, demultiplexer_1_out6, demultiplexer_1_out7,
       demultiplexer_2_out0, demultiplexer_2_out1, demultiplexer_3_out0, demultiplexer_3_out1,
       demultiplexer_3_out2, demultiplexer_3_out3, demultiplexer_3_out4, demultiplexer_3_out5,
       demultiplexer_3_out6, demultiplexer_3_out7, flags, hlt, jmp, ldi, lod, log, mul, multiplexer_1_out,
       multiplexer_14_out, N, nand_1_out, nop, NZ, or_1_out, or_2_out, or_3_out, or_4_out, or_6_out, RAM_WE,
       ret, RF_WE, rgb_video_1_p1, STATE0, STATE1, STATE2, STATE3, str, sub, Z;
  wire [1:0] adder_3_out, multiplexer_2_out, multiplexer_4_out, multiplexer_6_out, multiplexer_7_out, STATE_q;
  wire [7:0] adder_1_out, adder_2_out, adder_4_out, adder_5_out, and_14_out, DATA_BUFFER_q,
       multiplexer_3_out, multiplexer_5_out, multiplexer_8_out, multiplexer_9_out, multiplexer_10_out,
       multiplexer_11_out, multiplexer_12_out, multiplexer_13_out, multiplexer_15_out, multiplier_1_cout,
       multiplier_1_out, negator_1_out, nor_1_out, or_8_out, ram_1_dout, ram_2_dout, register_1_q,
       register_2_q, register_3_q, register_4_q, register_5_q, register_6_q, register_7_q, register_8_q,
       register_9_q, register_10_q, register_11_q, register_12_q, register_13_q, register_14_q,
       register_15_q, register_16_q, ROM_ADDR, subtractor_1_out, xor_1_out;
  wire [15:0] INST, ROM_OUT;
  wire [23:0] rgb_video_1_p7;

  and and_1 (and_1_out, STATE3, cal);
  and and_2 (and_2_out, ret, STATE2);
  and and_3 (and_3_out, cal, STATE3);
  and and_4 (and_4_out, jmp, STATE2);
  and and_5 (and_5_out, STATE2, ret);
  Multiplexer #(.select(2)) multiplexer_1 (
    .in0(Z), .in1(N), .in2(C), .in3(NZ), .out(multiplexer_1_out), .sel(INST[3:2]));
  or or_1 (or_1_out, cal, ret);
  and and_6 (and_6_out, STATE2, brh, multiplexer_1_out);
  Adder adder_1 (.a(register_1_q), .b(8'h1), .out(adder_1_out));  // open: cin, cout
  Subtractor subtractor_1 (.a(register_1_q), .b(8'h1), .out(subtractor_1_out));  // open: bin, bout
  Multiplexer #(.width(2)) multiplexer_2 (.in0(2'b00), .in1(2'b10), .out(multiplexer_2_out), .sel(and_2_out));
  or or_2 (or_2_out, and_6_out, and_3_out, and_4_out);
  Adder adder_2 (.a(8'h1), .b(ROM_ADDR), .out(adder_2_out));  // open: cin, cout
  Register register_1 (.D(multiplexer_3_out), .en(and_7_out), .clk(clk), .Q(register_1_q), .clr(Reset));
  Multiplexer #(.width(8)) multiplexer_3 (
    .in0(adder_1_out), .in1(subtractor_1_out), .out(multiplexer_3_out), .sel(ret));
  and and_7 (and_7_out, or_1_out, STATE1);
  Multiplexer #(.width(2)) multiplexer_4 (
    .in0(multiplexer_2_out), .in1(2'b01), .out(multiplexer_4_out), .sel(or_2_out));
  Multiplexer #(.select(2), .width(8)) multiplexer_5 (
    .in0(adder_2_out), .in1(INST[11:4]), .in2(ram_1_dout), .out(multiplexer_5_out), .sel(multiplexer_4_out));  // open: in3
  or or_3 (or_3_out, STATE0, and_4_out, and_1_out, and_6_out, and_5_out);
  and and_8 (and_8_out, cal, STATE1);
  Register PC (.D(multiplexer_5_out), .en(or_3_out), .clk(clk), .Q(ROM_ADDR), .clr(Reset));
  RAM #(.asyncread("true"), .clearpin("true")) ram_1 (
    .addr(register_1_q), .we(and_8_out), .oe(1'b1), .clk(clk), .din(ROM_ADDR), .dout(ram_1_dout), .clr(Reset));
  and and_9 (flags, or_4_out, STATE2);
  Register #(.width(16)) IR (.D(ROM_OUT), .en(STATE0), .clk(clk), .Q(INST), .clr(Reset));
  or or_4 (or_4_out, add, sub, mul, log);
  Adder #(.width(2)) adder_3 (.a(STATE_q), .b(2'b01), .out(adder_3_out));  // open: cin, cout
  Register #(.width(2)) STATE (.D(adder_3_out), .en(1'b1), .clk(clk), .Q(STATE_q), .clr(Reset));
  Decoder #(.select(4)) decoder_1 (
    .out0(nop), .out1(add), .out2(sub), .out3(mul), .out4(log), .out5(jmp), .out6(brh), .out7(lod),
    .out8(str), .out11(hlt), .out12(cal), .out13(ret), .out14(ldi), .sel(INST[15:12]));  // open: out9, out10, out15, en
  Decoder #(.select(2)) decoder_2 (
    .out0(STATE0), .out1(STATE1), .out2(STATE2), .out3(STATE3), .sel(STATE_q));  // open: en
  and and_10 (and_10_out, STATE2, str);
  buf or_5 (RAM_WE, and_10_out);  // OR_Gate
  or or_6 (or_6_out, lod, add, sub, mul, log, ldi);
  and and_11 (DB_WE, or_6_out, STATE2);
  and and_12 (RF_WE, or_6_out, STATE3);
  ROM #(.dataWidth(16)) rom_1 (.addr(ROM_ADDR), .data(ROM_OUT));
  Multiplexer #(.width(2)) multiplexer_6 (.in0(2'b00), .in1(2'b10), .out(multiplexer_6_out), .sel(lod));
  Clock clock_1 (.out(clock_1_out));
  Multiplexer #(.width(2)) multiplexer_7 (.in0(multiplexer_6_out), .in1(2'b01), .out(multiplexer_7_out), .sel(ldi));
  nand nand_1 (nand_1_out, hlt, STATE2);
  Multiplexer #(.select(2), .width(8)) multiplexer_8 (
    .in0(multiplexer_15_out), .in1(INST[11:4]), .in2(multiplexer_11_out), .in3({8{1'b0}}),
    .out(multiplexer_8_out), .sel(multiplexer_7_out));
  and and_13 (and_13_out, clock_1_out, Run, nand_1_out);
  Register DATA_BUFFER (.D(multiplexer_8_out), .en(DB_WE), .clk(clk), .Q(DATA_BUFFER_q), .clr(Reset));
  or or_7 (clk, and_13_out, Manual_mode);
  Demultiplexer #(.select(3)) demultiplexer_1 (
    .out1(demultiplexer_1_out1), .out2(demultiplexer_1_out2), .out3(demultiplexer_1_out3),
    .out4(demultiplexer_1_out4), .out5(demultiplexer_1_out5), .out6(demultiplexer_1_out6),
    .out7(demultiplexer_1_out7), .in(RF_WE), .sel(INST[2:0]));  // open: out0
  Register register_2 (.D(DATA_BUFFER_q), .en(demultiplexer_1_out1), .clk(clk), .Q(register_2_q), .clr(Reset));
  Register register_3 (.D(DATA_BUFFER_q), .en(demultiplexer_1_out2), .clk(clk), .Q(register_3_q), .clr(Reset));
  Register register_4 (.D(DATA_BUFFER_q), .en(demultiplexer_1_out3), .clk(clk), .Q(register_4_q), .clr(Reset));
  Register register_5 (.D(DATA_BUFFER_q), .en(demultiplexer_1_out4), .clk(clk), .Q(register_5_q), .clr(Reset));
  Register register_6 (.D(DATA_BUFFER_q), .en(demultiplexer_1_out5), .clk(clk), .Q(register_6_q), .clr(Reset));
  Register register_7 (.D(DATA_BUFFER_q), .en(demultiplexer_1_out6), .clk(clk), .Q(register_7_q), .clr(Reset));
  Register register_8 (.D(DATA_BUFFER_q), .en(demultiplexer_1_out7), .clk(clk), .Q(register_8_q), .clr(Reset));
  Multiplexer #(.select(3), .width(8)) multiplexer_9 (
    .in0({8{1'b0}}), .in1(register_2_q), .in2(register_3_q), .in3(register_4_q), .in4(register_5_q),
    .in5(register_6_q), .in6(register_7_q), .in7(register_8_q), .out(multiplexer_9_out), .sel(INST[11:9]));
  // Probe on multiplexer_9_out
  Multiplexer #(.select(3), .width(8)) multiplexer_10 (
    .in0({8{1'b0}}), .in1(register_2_q), .in2(register_3_q), .in3(register_4_q), .in4(register_5_q),
    .in5(register_6_q), .in6(register_7_q), .in7(register_8_q), .out(multiplexer_10_out), .sel(INST[8:6]));
  Multiplexer #(.width(8)) multiplexer_11 (
    .in0(ram_2_dout), .in1(multiplexer_12_out), .out(multiplexer_11_out), .sel(and_15_out));
  // Probe on multiplexer_10_out
  Multiplexer #(.select(3), .width(8)) multiplexer_12 (
    .in0(in_3), .in1(in_5), .in2(in_6), .in3(in_7), .in4(in_8), .in5(in_9), .in6(in_10), .in7(in_11),
    .out(multiplexer_12_out), .sel(multiplexer_9_out[2:0]));
  assign and_14_out = multiplexer_9_out & multiplexer_10_out;  // AND_Gate and_14, 8 bits wide
  assign or_8_out = multiplexer_9_out | multiplexer_10_out;  // OR_Gate or_8, 8 bits wide
  Demultiplexer demultiplexer_2 (
    .out0(demultiplexer_2_out0), .out1(demultiplexer_2_out1), .in(RAM_WE), .sel(and_15_out));
  and and_15 (and_15_out, multiplexer_9_out[3], multiplexer_9_out[4], multiplexer_9_out[5], multiplexer_9_out[6], multiplexer_9_out[7]);
  RAM #(.clearpin("true")) ram_2 (
    .addr(multiplexer_9_out), .we(demultiplexer_2_out0), .oe(1'b1), .clk(clk), .din(multiplexer_10_out),
    .dout(ram_2_dout), .clr(Reset));
  assign nor_1_out = ~(multiplexer_9_out | multiplexer_10_out);  // NOR_Gate nor_1, 8 bits wide
  Multiplexer #(.select(3), .width(8)) multiplexer_13 (
    .in0(and_14_out), .in1(or_8_out), .in2(nor_1_out), .in3(xor_1_out), .in4({1'b0, multiplexer_9_out[7:1]}),
    .in5({8{1'b0}}), .in6({8{1'b0}}), .in7({8{1'b0}}), .out(multiplexer_13_out), .sel(INST[5:3]));
  assign xor_1_out = multiplexer_9_out ^ multiplexer_10_out;  // XOR_Gate xor_1, 8 bits wide
  Negator negator_1 (.in(multiplexer_10_out), .out(negator_1_out));
  Demultiplexer #(.select(3)) demultiplexer_3 (
    .out0(demultiplexer_3_out0), .out1(demultiplexer_3_out1), .out2(demultiplexer_3_out2),
    .out3(demultiplexer_3_out3), .out4(demultiplexer_3_out4), .out5(demultiplexer_3_out5),
    .out6(demultiplexer_3_out6), .out7(demultiplexer_3_out7), .in(demultiplexer_2_out1),
    .sel(multiplexer_9_out[2:0]));
  Multiplexer #(.select(2)) multiplexer_14 (
    .in0(1'b0), .in1(adder_4_cout), .in2(adder_5_cout), .in3(multiplier_1_cout[0]), .out(multiplexer_14_out),
    .sel(INST[13:12]));
  Adder adder_4 (.a(multiplexer_9_out), .b(multiplexer_10_out), .out(adder_4_out), .cout(adder_4_cout));  // open: cin
  Adder adder_5 (.a(multiplexer_9_out), .b(negator_1_out), .out(adder_5_out), .cout(adder_5_cout));  // open: cin
  Multiplier multiplier_1 (
    .a(multiplexer_9_out), .b(multiplexer_10_out), .out(multiplier_1_out), .cout(multiplier_1_cout));  // open: cin
  Register register_9 (.D(multiplexer_10_out), .en(demultiplexer_3_out0), .clk(clk), .Q(register_9_q), .clr(Reset));
  Register register_10 (.D(multiplexer_10_out), .en(demultiplexer_3_out1), .clk(clk), .Q(register_10_q), .clr(Reset));
  Register register_11 (.D(multiplexer_10_out), .en(demultiplexer_3_out2), .clk(clk), .Q(register_11_q), .clr(Reset));
  Register register_12 (.D(multiplexer_10_out), .en(demultiplexer_3_out3), .clk(clk), .Q(register_12_q), .clr(Reset));
  Multiplexer #(.select(3), .width(8)) multiplexer_15 (
    .in0({8{1'b0}}), .in1(adder_4_out), .in2(adder_5_out), .in3(multiplier_1_out), .in4(multiplexer_13_out),
    .in5({8{1'b0}}), .in6({8{1'b0}}), .in7({8{1'b0}}), .out(multiplexer_15_out), .sel(INST[14:12]));
  Comparator comparator_1 (.a(multiplexer_15_out), .b({8{1'b0}}), .eq(comparator_1_eq));  // open: gt, lt
  Register register_13 (.D(multiplexer_10_out), .en(demultiplexer_3_out4), .clk(clk), .Q(register_13_q), .clr(Reset));
  Register register_14 (.D(multiplexer_10_out), .en(demultiplexer_3_out5), .clk(clk), .Q(register_14_q), .clr(Reset));
  Register register_15 (.D(multiplexer_10_out), .en(demultiplexer_3_out6), .clk(clk), .Q(register_15_q), .clr(Reset));
  Register register_16 (.D(multiplexer_10_out), .en(demultiplexer_3_out7), .clk(clk), .Q(register_16_q), .clr(Reset));
  Register #(.width(1)) u_N (.D(multiplexer_15_out[7]), .en(flags), .clk(clk), .Q(N), .clr(Reset));
  Register #(.width(1)) u_Z (.D(comparator_1_eq), .en(flags), .clk(clk), .Q(Z), .clr(Reset));
  Register #(.width(1)) u_C (.D(multiplexer_14_out), .en(flags), .clk(clk), .Q(C), .clr(Reset));
  // Probe on register_9_q
  // Probe on register_10_q
  // Probe on register_11_q
  // Probe on register_12_q
  // Probe on register_13_q
  // Probe on register_14_q
  // Probe on register_15_q
  // Probe on register_16_q
  not not_1 (NZ, Z);
  // RGB_Video #(.height(256), .scale(1), .width(256)) rgb_video_1: pin names not known; wires that end beside it: rgb_video_1_p1, register_11_q[1], register_11_q[0], register_9_q, register_10_q, {24{1'b1}}, rgb_video_1_p7
  or or_9 (rgb_video_1_p1, register_11_q[2], Reset);
  Multiplexer #(.width(24)) multiplexer_16 (
    .in0({24{1'b1}}), .in1({24{1'b0}}), .out(rgb_video_1_p7), .sel(register_11_q[3]));

  // Notes on the sheet:
  //   Jump/branch logic
  //   Call stack
  //   Operation decoder and logic
  //   State processing
  //   INSTRUCTON ROM
  //   Clock
  //   REGISTER FILE
  //   Input ports
  //   RAM
  //   ALU
  //   Output ports
  //   FLAGS
endmodule
