// Logisim project vn8.circ as structural Verilog: 2 circuits, main circuit main
module main (
  input  [15:0] in_1,
  input  [7:0] in_2,
  input  [7:0] in_3,
  input  Run,
  input  Manual_mode,
  input  Reset,
  input  [7:0] in_7,
  input  [7:0] in_8,
  input  [7:0] in_9,
  input  [7:0] in_10,
  input  [7:0] in_11,
  input  [7:0] in_12
);

  wire add, adder_4_cout, adder_5_cout, adi, and_1_out, and_2_out, and_3_out, and_5_out, and_9_out,
       and_10_out, and_11_out, and_13_out, and_14_out, brh, C, cal, clk, clock_1_out, comparator_1_eq, DB_WE,
       demultiplexer_1_out1, demultiplexer_1_out2, demultiplexer_1_out3, demultiplexer_1_out4,
       demultiplexer_1_out5, demultiplexer_1_out6, demultiplexer_1_out7, demultiplexer_3_out0,
       demultiplexer_4_out0, demultiplexer_4_out1, demultiplexer_5_out0, demultiplexer_5_out1,
       demultiplexer_5_out2, demultiplexer_5_out3, demultiplexer_5_out4, demultiplexer_5_out5,
       demultiplexer_5_out6, demultiplexer_5_out7, flags, hlt, ILOD, ISTR, jmp, ldi, lod, log, mul,
       multiplexer_16_out, multiplexer_17_out, multiplexer_18_out, N, nand_1_out, NC, nop, nor_1_out,
       not_1_out, NZ, or_1_out, or_2_out, or_3_out, or_5_out, pc_control_logic_1_pc_we, RAM_WE, ret, RF_WE,
       rgb_video_1_p1, rgb_video_1_p2, STATE0, STATE1, STATE2, STATE3, str, sub, Z;
  wire [1:0] adder_3_out, multiplexer_4_out, multiplexer_5_out, pc_control_logic_1_pc_mux, STATE_q;
  wire [2:0] multiplexer_7_out, multiplexer_11_out, multiplexer_19_out;
  wire [3:0] adder_1_out, multiplexer_1_out, register_1_q, subtractor_1_out;
  wire [7:0] adder_4_out, adder_5_out, and_12_out, DATA_BUFFER_q, demultiplexer_2_out0, demultiplexer_2_out1,
       multiplexer_6_out, multiplexer_8_out, multiplexer_9_out, multiplexer_14_out, multiplexer_15_out,
       multiplexer_20_out, multiplexer_21_out, multiplier_1_cout, multiplier_1_out, nor_2_out, not_2_out,
       or_8_out, or_10_out, ram_3_dout, RAMDB, register_2_q, register_3_q, register_4_q, register_5_q,
       register_6_q, register_7_q, register_8_q, register_10_q, register_11_q, register_12_q, register_13_q,
       register_14_q, register_15_q, register_16_q, register_17_q, xor_1_out, Y_out;
  wire [15:0] adder_2_out, INST, multiplexer_2_out, PC_q, ram_1_dout, ram_2_dout, RAMADDR, ROM_ADDR, ROM_OUT;
  wire [15:8] RARB;

  PC_control_logic pc_control_logic_1 (
    .INST(INST), .STATE0(STATE0), .STATE2(STATE2), .STATE3(STATE3), .jmp(jmp), .cal(cal), .ret(ret),
    .brh(brh), .z(Z), .n(N), .c(C), .nz(NZ), .nc(NC), .pc_mux(pc_control_logic_1_pc_mux),
    .pc_we(pc_control_logic_1_pc_we));
  or or_1 (or_1_out, cal, ret);
  Adder #(.width(4)) adder_1 (.a(register_1_q), .b(4'b0001), .out(adder_1_out));  // open: cin, cout
  Subtractor #(.width(4)) subtractor_1 (.a(register_1_q), .b(4'b0001), .out(subtractor_1_out));  // open: bin, bout
  Adder #(.width(16)) adder_2 (.a(16'h1), .b(PC_q), .out(adder_2_out));  // open: cin, cout
  Register #(.width(4)) register_1 (.D(multiplexer_1_out), .en(and_1_out), .clk(clk), .Q(register_1_q), .clr(Reset));
  Multiplexer #(.width(4)) multiplexer_1 (
    .in0(adder_1_out), .in1(subtractor_1_out), .out(multiplexer_1_out), .sel(ret));
  and and_1 (and_1_out, or_1_out, STATE1);
  Multiplexer #(.select(2), .width(16)) multiplexer_2 (
    .in0(adder_2_out), .in1(ROM_OUT), .in2(ram_1_dout), .in3({RARB, RAMADDR[7:0]}), .out(multiplexer_2_out),
    .sel(pc_control_logic_1_pc_mux));
  and and_2 (and_2_out, cal, STATE1);
  Register #(.width(16)) PC (.D(multiplexer_2_out), .en(pc_control_logic_1_pc_we), .clk(clk), .Q(PC_q), .clr(Reset));
  RAM #(.addrWidth(4), .asyncread("true"), .clearpin("true"), .dataWidth(16)) ram_1 (
    .addr(register_1_q), .we(and_2_out), .oe(1'b1), .clk(clk), .din(PC_q), .dout(ram_1_dout), .clr(Reset));
  Multiplexer #(.width(16)) multiplexer_3 (.in0(PC_q), .in1(RAMADDR), .out(ROM_ADDR), .sel(or_2_out));
  or or_2 (or_2_out, and_3_out, ISTR);
  and and_3 (and_3_out, ILOD, STATE2);
  and and_4 (flags, or_3_out, STATE2);
  Register #(.width(16)) IR (.D(ROM_OUT), .en(STATE0), .clk(clk), .Q(INST), .clr(Reset));
  or or_3 (or_3_out, mul, add, sub, log, adi);
  Adder #(.width(2)) adder_3 (.a(STATE_q), .b(2'b01), .out(adder_3_out));  // open: cin, cout
  Register #(.width(2)) STATE (.D(adder_3_out), .en(1'b1), .clk(clk), .Q(STATE_q), .clr(Reset));
  Decoder #(.select(4)) decoder_1 (
    .out0(nop), .out1(add), .out2(sub), .out3(mul), .out4(log), .out5(jmp), .out6(brh), .out7(lod),
    .out8(str), .out9(adi), .out11(hlt), .out12(cal), .out13(ret), .out14(ldi), .sel(INST[15:12]));  // open: out10, out15, en
  Decoder #(.select(2)) decoder_2 (
    .out0(STATE0), .out1(STATE1), .out2(STATE2), .out3(STATE3), .sel(STATE_q));  // open: en
  and and_5 (and_5_out, STATE3, str);
  buf or_4 (RAM_WE, and_5_out);  // OR_Gate
  or or_5 (or_5_out, lod, add, sub, mul, log, ldi, adi);
  and and_6 (DB_WE, or_5_out, STATE2);
  and and_7 (RF_WE, or_5_out, STATE3);
  Multiplexer #(.width(2)) multiplexer_4 (.in0(2'b00), .in1(2'b10), .out(multiplexer_4_out), .sel(lod));
  Multiplexer #(.width(2)) multiplexer_5 (.in0(multiplexer_4_out), .in1(2'b01), .out(multiplexer_5_out), .sel(ldi));
  Multiplexer #(.select(2), .width(8)) multiplexer_6 (
    .in0(multiplexer_20_out), .in1(INST[11:4]), .in2(multiplexer_8_out), .in3({8{1'b0}}),
    .out(multiplexer_6_out), .sel(multiplexer_5_out));
  Multiplexer #(.width(3)) multiplexer_7 (.in0(INST[2:0]), .in1(INST[11:9]), .out(multiplexer_7_out), .sel(adi));
  Register DATA_BUFFER (.D(multiplexer_6_out), .en(DB_WE), .clk(clk), .Q(DATA_BUFFER_q), .clr(Reset));
  Demultiplexer #(.select(3)) demultiplexer_1 (
    .out1(demultiplexer_1_out1), .out2(demultiplexer_1_out2), .out3(demultiplexer_1_out3),
    .out4(demultiplexer_1_out4), .out5(demultiplexer_1_out5), .out6(demultiplexer_1_out6),
    .out7(demultiplexer_1_out7), .in(RF_WE), .sel(multiplexer_7_out));  // open: out0
  Demultiplexer #(.width(8)) demultiplexer_2 (
    .out0(demultiplexer_2_out0), .out1(demultiplexer_2_out1), .in(RAMDB), .sel(INST[4]));
  not not_1 (not_1_out, INST[4]);
  RAM #(.addrWidth(16), .asyncread("true"), .byteenables("byteEnables"), .dataWidth(16)) ram_2 (
    .addr(ROM_ADDR), .we(ISTR), .oe(1'b1), .clk(clk), .din({demultiplexer_2_out1, demultiplexer_2_out0}),
    .dout(ram_2_dout), .be1(INST[4]), .be0(not_1_out));
  and and_8 (ILOD, INST[3], lod);
  Register register_2 (.D(DATA_BUFFER_q), .en(demultiplexer_1_out1), .clk(clk), .Q(register_2_q), .clr(Reset));
  Register register_3 (.D(DATA_BUFFER_q), .en(demultiplexer_1_out2), .clk(clk), .Q(register_3_q), .clr(Reset));
  Register register_4 (.D(DATA_BUFFER_q), .en(demultiplexer_1_out3), .clk(clk), .Q(register_4_q), .clr(Reset));
  Register register_5 (.D(DATA_BUFFER_q), .en(demultiplexer_1_out4), .clk(clk), .Q(register_5_q), .clr(Reset));
  Register register_6 (.D(DATA_BUFFER_q), .en(demultiplexer_1_out5), .clk(clk), .Q(register_6_q), .clr(Reset));
  Register register_7 (.D(DATA_BUFFER_q), .en(demultiplexer_1_out6), .clk(clk), .Q(register_7_q), .clr(Reset));
  Register register_8 (.D(DATA_BUFFER_q), .en(demultiplexer_1_out7), .clk(clk), .Q(register_8_q), .clr(Reset));
  assign ROM_OUT = in_1 | ram_2_dout;  // OR_Gate or_6, 16 bits wide
  Multiplexer #(.width(8)) multiplexer_8 (
    .in0(multiplexer_14_out), .in1(multiplexer_9_out), .out(multiplexer_8_out), .sel(ILOD));
  Multiplexer #(.width(8)) multiplexer_9 (
    .in0(ROM_OUT[7:0]), .in1(ROM_OUT[15:8]), .out(multiplexer_9_out), .sel(INST[4]));
  Clock clock_1 (.out(clock_1_out));
  Multiplexer #(.select(3), .width(8)) multiplexer_10 (
    .in0({8{1'b0}}), .in1(register_2_q), .in2(register_3_q), .in3(register_4_q), .in4(register_5_q),
    .in5(register_6_q), .in6(register_7_q), .in7(register_8_q), .out(RAMADDR[7:0]), .sel(multiplexer_11_out));
  // Probe on RAMADDR[7:0]
  Multiplexer #(.width(3)) multiplexer_11 (
    .in0(INST[11:9]), .in1(INST[2:0]), .out(multiplexer_11_out), .sel(and_11_out));
  Multiplexer #(.select(3), .width(8)) multiplexer_12 (
    .in0({8{1'b0}}), .in1(register_2_q), .in2(register_3_q), .in3(register_4_q), .in4(register_5_q),
    .in5(register_6_q), .in6(register_7_q), .in7(register_8_q), .out(RARB), .sel(INST[8:6]));
  Multiplexer #(.width(8)) multiplexer_13 (.in0(RARB), .in1(INST[7:0]), .out(RAMADDR[15:8]), .sel(adi));
  Multiplexer #(.width(8)) multiplexer_14 (
    .in0(ram_3_dout), .in1(multiplexer_21_out), .out(multiplexer_14_out), .sel(and_14_out));
  and and_9 (and_9_out, str, STATE1);
  nand nand_1 (nand_1_out, hlt, STATE2);
  // Probe on RAMADDR[15:8]
  Register register_9 (.D(RAMADDR[7:0]), .en(and_9_out), .clk(clk), .Q(RAMDB), .clr(Reset));
  and and_10 (and_10_out, clock_1_out, Run, nand_1_out);
  and and_11 (and_11_out, STATE1, str);
  assign and_12_out = RAMADDR[7:0] & RAMADDR[15:8];  // AND_Gate and_12, 8 bits wide
  Demultiplexer demultiplexer_3 (.out0(demultiplexer_3_out0), .out1(ISTR), .in(RAM_WE), .sel(INST[3]));
  or or_7 (clk, and_10_out, Manual_mode);
  assign or_8_out = RAMADDR[7:0] | RAMADDR[15:8];  // OR_Gate or_8, 8 bits wide
  nor nor_1 (nor_1_out, RAMADDR[15], RAMADDR[14], RAMADDR[13], RAMADDR[12], RAMADDR[10], RAMADDR[11], RAMADDR[9], RAMADDR[8]);
  and and_13 (and_13_out, RAMADDR[7], RAMADDR[6], RAMADDR[5], RAMADDR[4], RAMADDR[3]);
  Demultiplexer demultiplexer_4 (
    .out0(demultiplexer_4_out0), .out1(demultiplexer_4_out1), .in(demultiplexer_3_out0), .sel(and_14_out));
  RAM #(.addrWidth(16), .clearpin("true")) ram_3 (
    .addr(RAMADDR), .we(demultiplexer_4_out0), .oe(1'b1), .clk(clk), .din(RAMDB), .dout(ram_3_dout),
    .clr(Reset));
  assign nor_2_out = ~(RAMADDR[7:0] | RAMADDR[15:8]);  // NOR_Gate nor_2, 8 bits wide
  Multiplexer #(.select(3), .width(8)) multiplexer_15 (
    .in0(and_12_out), .in1(or_8_out), .in2(nor_2_out), .in3(xor_1_out), .in4({1'b0, RAMADDR[7:1]}),
    .in5({8{1'b0}}), .in6({8{1'b0}}), .in7({8{1'b0}}), .out(multiplexer_15_out), .sel(INST[5:3]));
  and and_14 (and_14_out, and_13_out, nor_1_out);
  assign xor_1_out = RAMADDR[7:0] ^ RAMADDR[15:8];  // XOR_Gate xor_1, 8 bits wide
  assign not_2_out = ~RAMADDR[15:8];  // NOT_Gate not_2, 8 bits wide
  Demultiplexer #(.select(3)) demultiplexer_5 (
    .out0(demultiplexer_5_out0), .out1(demultiplexer_5_out1), .out2(demultiplexer_5_out2),
    .out3(demultiplexer_5_out3), .out4(demultiplexer_5_out4), .out5(demultiplexer_5_out5),
    .out6(demultiplexer_5_out6), .out7(demultiplexer_5_out7), .in(demultiplexer_4_out1), .sel(RAMADDR[2:0]));
  Multiplexer #(.select(2)) multiplexer_16 (
    .in0(1'b0), .in1(adder_4_cout), .in2(adder_5_cout), .in3(multiplier_1_cout[0]), .out(multiplexer_16_out),
    .sel(INST[13:12]));
  Multiplexer multiplexer_17 (.in0(1'b0), .in1(C), .out(multiplexer_17_out), .sel(INST[3]));
  Multiplexer multiplexer_18 (.in0(1'b1), .in1(C), .out(multiplexer_18_out), .sel(INST[3]));
  Adder adder_4 (.a(RAMADDR[7:0]), .b(RAMADDR[15:8]), .out(adder_4_out), .cin(multiplexer_17_out), .cout(adder_4_cout));
  Adder adder_5 (.a(RAMADDR[7:0]), .b(not_2_out), .out(adder_5_out), .cin(multiplexer_18_out), .cout(adder_5_cout));
  Multiplier multiplier_1 (
    .a(RAMADDR[7:0]), .b(RAMADDR[15:8]), .out(multiplier_1_out), .cout(multiplier_1_cout));  // open: cin
  Multiplexer #(.width(3)) multiplexer_19 (.in0(INST[14:12]), .in1(3'b001), .out(multiplexer_19_out), .sel(adi));
  Register register_10 (.D(RAMDB), .en(demultiplexer_5_out0), .clk(clk), .Q(register_10_q), .clr(Reset));
  Register register_11 (.D(RAMDB), .en(demultiplexer_5_out1), .clk(clk), .Q(register_11_q), .clr(Reset));
  Register register_12 (.D(RAMDB), .en(demultiplexer_5_out2), .clk(clk), .Q(register_12_q), .clr(Reset));
  Register register_13 (.D(RAMDB), .en(demultiplexer_5_out3), .clk(clk), .Q(register_13_q), .clr(Reset));
  Multiplexer #(.select(3), .width(8)) multiplexer_20 (
    .in0({8{1'b0}}), .in1(adder_4_out), .in2(adder_5_out), .in3(multiplier_1_out), .in4(multiplexer_15_out),
    .in5({8{1'b0}}), .in6({8{1'b0}}), .in7({8{1'b0}}), .out(multiplexer_20_out), .sel(multiplexer_19_out));
  Comparator comparator_1 (.a(multiplexer_20_out), .b({8{1'b0}}), .eq(comparator_1_eq));  // open: gt, lt
  Register register_14 (.D(RAMDB), .en(demultiplexer_5_out4), .clk(clk), .Q(register_14_q), .clr(Reset));
  Register register_15 (.D(RAMDB), .en(demultiplexer_5_out5), .clk(clk), .Q(register_15_q), .clr(Reset));
  Register register_16 (.D(RAMDB), .en(demultiplexer_5_out6), .clk(clk), .Q(register_16_q), .clr(Reset));
  Register register_17 (.D(RAMDB), .en(demultiplexer_5_out7), .clk(clk), .Q(register_17_q), .clr(Reset));
  Register #(.width(1)) u_N (.D(multiplexer_20_out[7]), .en(flags), .clk(clk), .Q(N), .clr(Reset));
  Register #(.width(1)) u_Z (.D(comparator_1_eq), .en(flags), .clk(clk), .Q(Z), .clr(Reset));
  Register #(.width(1)) u_C (.D(multiplexer_16_out), .en(flags), .clk(clk), .Q(C), .clr(Reset));
  // Probe on register_10_q
  // Probe on register_11_q
  // Probe on register_12_q
  // Probe on register_13_q
  // Probe on register_14_q
  // Probe on register_15_q
  // Probe on register_16_q
  // Probe on register_17_q
  not not_3 (NZ, Z);
  not not_4 (NC, C);
  // RGB_Video #(.cursor("No Cursor")) rgb_video_1: pin names not known; wires that end beside it: rgb_video_1_p1, rgb_video_1_p2, rgb_video_1_p2, register_10_q[6:0], register_11_q[6:0], {register_12_q[7:5], register_12_q[7:5], register_12_q[7:6], register_12_q[4:2], register_12_q[4:2], register_12_q[4:3], register_12_q[1:0], register_12_q[1:0], register_12_q[1:0], register_12_q[1:0]}
  not not_5 (rgb_video_1_p2, demultiplexer_5_out2);
  or or_9 (rgb_video_1_p1, register_10_q[7], Reset);
  Button button_1 (.out(Y_out[4]));
  Button button_2 (.out(Y_out[7]));
  Button button_3 (.out(Y_out[5]));
  Button button_4 (.out(Y_out[6]));
  Button A (.out(Y_out[2]));
  Button B (.out(Y_out[1]));
  Button X (.out(Y_out[3]));
  Button Y (.out(Y_out[0]));
  assign or_10_out = Y_out | in_2;  // OR_Gate or_10, 8 bits wide
  Multiplexer #(.select(3), .width(8)) multiplexer_21 (
    .in0(or_10_out), .in1(in_3), .in2(in_7), .in3(in_8), .in4(in_9), .in5(in_10), .in6(in_11), .in7(in_12),
    .out(multiplexer_21_out), .sel(RAMADDR[2:0]));

  // Other names for the same wires on the sheet: RARB[7:0] = RAMADDR[7:0]; SI = INST[3]; LH = INST[4]

  // Notes on the sheet:
  //   Jump/branch logic
  //   Call stack
  //   Operation decoder and logic
  //   State processing
  //   INSTRUCTON RAM
  //   REGISTER FILE
  //   Clock
  //   ALU
  //   RAM
  //   Output ports
  //   FLAGS
  //   Input ports
endmodule

module PC_control_logic (
  input  STATE0,
  input  STATE2,
  input  STATE3,
  input  jmp,
  input  cal,
  input  ret,
  input  brh,
  input  z,
  input  n,
  input  c,
  input  nz,
  input  nc,
  input  [15:0] INST,
  output [1:0] pc_mux,
  output pc_we
);

  wire and_1_out, and_2_out, and_3_out, and_4_out, and_5_out, and_6_out, and_7_out, and_8_out, and_9_out,
       and_10_out, multiplexer_1_out, not_1_out, or_1_out, or_2_out;
  wire [1:0] multiplexer_2_out, multiplexer_3_out, multiplexer_4_out;

  Multiplexer #(.select(3)) multiplexer_1 (
    .in0(z), .in1(n), .in2(c), .in3(nz), .in4(nc), .out(multiplexer_1_out), .sel(INST[3:1]));  // open: in5, in6, in7
  and and_1 (and_1_out, jmp, STATE3);
  and and_2 (and_2_out, cal, STATE3);
  and and_3 (and_3_out, brh, STATE2);
  and and_4 (and_4_out, jmp, STATE3);
  and and_5 (and_5_out, STATE3, cal);
  and and_6 (and_6_out, brh, STATE2, multiplexer_1_out);
  and and_7 (and_7_out, ret, STATE2);
  not not_1 (not_1_out, multiplexer_1_out);
  or or_1 (or_1_out, and_1_out, and_2_out, and_3_out);
  and and_8 (and_8_out, or_1_out, ~INST[4]);  // AND_Gate
  and and_9 (and_9_out, brh, STATE2, and_8_out, not_1_out);
  Multiplexer #(.width(2)) multiplexer_2 (.in0(2'b00), .in1(2'b10), .out(multiplexer_2_out), .sel(and_7_out));
  Multiplexer #(.width(2)) multiplexer_3 (
    .in0(multiplexer_2_out), .in1(2'b01), .out(multiplexer_3_out), .sel(or_2_out));
  Multiplexer #(.width(2)) multiplexer_4 (
    .in0(multiplexer_3_out), .in1(2'b00), .out(multiplexer_4_out), .sel(and_9_out));
  or or_2 (or_2_out, and_4_out, and_5_out, and_6_out);
  Multiplexer #(.width(2)) multiplexer_5 (.in0(multiplexer_4_out), .in1(2'b11), .out(pc_mux), .sel(and_10_out));
  and and_10 (and_10_out, or_2_out, INST[4]);
  or or_3 (pc_we, and_4_out, and_5_out, and_6_out, STATE0, and_7_out, and_9_out);
endmodule
